# Fritzing sketch Untitled Sketch (saved by Fritzing 1.0.6)
breadboards: 1

parts:
  Part1 = Arduino Uno (Rev3)
  VCC1 = Battery [internal_resistance=0.1Ω]
  Part2 = InvenSense MPU6050
  L298N1 = L298N DC motor driver
  M1 = gear-motor
  M2 = gear-motor

nets:
  N1: Part1.A4/SDA, Part2.SDA
  N2: Part1.A5/SCL, Part2.SCL
  N3: Part1.D8, L298N1.IN2
  N4: Part1.D9_PWM, L298N1.IN1
  N5: Part1.D10_PWM/SS, L298N1.ENA
  GND: Part1.GND, VCC1.-, Part2.GND, L298N1.GND
  N6: Part1.D2, Part2.INT
  N7: Part1.D5_PWM, L298N1.ENB
  N8: Part1.D6_PWM, L298N1.IN4
  N9: Part1.D7, L298N1.IN3
  5V: Part1.5V, Part2.VCC
  VIN: Part1.VIN, VCC1.+, L298N1.12V
  N10: L298N1.OUT1, M2.pin_2
  N11: L298N1.OUT2, M2.pin_1
  N12: L298N1.OUT3, M1.pin_1
  N13: L298N1.OUT4, M1.pin_2

custom parts:
  L298N DC motor driver: 2x DC motor driver with 78M05 positive voltage regulator (7..35 V) L298N: max 46 V, 2 A Set 5 V Enable jumper to enable 5 V regultor (needed for the L298N) and +5 V output at screw terminal or supply external +5 V at screw terminal Set ENA and/or ENB to +5 V to enable motor permanently or supply ENA and/or ENB with PWM signal IN1 and IN2 set rotation directory for motor A (OUT1/OUT2) IN2 and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
